# Fritzing sketch SideKickV3 (saved by Fritzing 0.9.6b)
circuit board: 6.95cm x 8.2cm
breadboards: 1

parts:
  ULN2803A = ULN2803A [package=THT]
  Front_Limit_Switch = YL-99 Limit switch and LED
  Rear_Limit_Switch = YL-99 Limit switch and LED
  Upper_Stepper_Motor = Stepper Motor - Bipolar
  Lower_Stepper_Motor = Stepper Motor - Bipolar
  Purge_Button = Momentary Switch [package=ksa_sealed_tac_switch]
  Pump_1 = Piezo Speaker
  Pump_2 = Piezo Speaker
  Pump_3 = Piezo Speaker
  Pump_4 = Piezo Speaker
  Pico = Raspberry Pi Pico
  Power_Jack = Power Jack [package=power_jack_pth_lock]
  P1 = Header 1 [package=1x01_offset]
  JP2 = Header 1 [package=1x01_offset]
  P2 = Header 1 [package=1x01_offset]
  JP4 = Header 1 [package=1x01_offset]
  P3 = Header 1 [package=1x01_offset]
  JP6 = Header 1 [package=1x01_offset]
  P4 = Header 1 [package=1x01_offset]
  JP8 = Header 1 [package=1x01_offset]
  Purge = Header 1 [package=1x01_offset]
  Schrier_Lab_Fordham_University = Header 1 [package=1x01_offset]
  F_Lim = Header 1 [package=1x01_offset]
  https_//github_com/rodolfokeesey/Liquid-Handler = Header 1 [package=1x01_offset]
  R_Lim = Header 1 [package=1x01_offset]
  SideKick_V1 = Header 1 [package=1x01_offset]
  Upper_Mot = Header 1 [package=1x01_offset]
  JP16 = Header 1 [package=1x01_offset]
  JP17 = Header 1 [package=1x01_offset]
  JP18 = Header 1 [package=1x01_offset]
  VBUS = Header 1 [package=1x01_offset]
  VSS = Header 1 [package=1x01_offset]
  3V3_EN = Header 1 [package=1x01_offset]
  ADC = Header 1 [package=1x01_offset]
  GP28 = Header 1 [package=1x01_offset]
  RUN = Header 1 [package=1x01_offset]
  12V = Header 1 [package=1x01_offset]
  AGND = Header 1 [package=1x01_offset]
  PSU_GND = Header 1 [package=1x01_offset]
  Lower_Mot = Header 1 [package=1x01_offset]
  JP20 = Header 1 [package=1x01_offset]
  JP21 = Header 1 [package=1x01_offset]
  JP22 = Header 1 [package=1x01_offset]
  Lower_Driver = TMC2209 [package=THT]
  Upper_Driver = TMC2209 [package=THT]
  3V3 = Header 1 [package=1x01_offset]

nets:
  N1: ULN2803A.In_1, Pico.pin_32
  N2: ULN2803A.In_2, Pico.pin_31
  N3: ULN2803A.In_3, Pico.pin_29
  N4: ULN2803A.In_4, Pico.pin_27
  GND: ULN2803A.0V, Front_Limit_Switch.OUT, Rear_Limit_Switch.OUT, Purge_Button.1, Pico.pin_3, Pico.pin_8, Pico.pin_13, Pico.pin_18, Pico.pin_23, Pico.pin_28, Pico.pin_33, Pico.pin_38, Power_Jack.GND, Purge.1, F_Lim.1, R_Lim.1, AGND.1, PSU_GND.1, Lower_Driver.GND_Logic, Lower_Driver.GND, Upper_Driver.GND_Logic, Upper_Driver.GND
  N5: ULN2803A.COM_-_Common, Pump_1.pin2, Pump_2.pin2, Pump_3.pin2, Pump_4.pin2, Power_Jack.PWR, JP2.1, JP4.1, JP6.1, JP8.1, 12V.1, Lower_Driver.VM, Upper_Driver.VM
  N6: ULN2803A.Out_4, Pump_4.pin1, P4.1
  N7: ULN2803A.Out_3, Pump_3.pin1, P3.1
  N8: ULN2803A.Out_2, Pump_2.pin1, P2.1
  N9: ULN2803A.Out_1, Pump_1.pin1, P1.1
  N10: Front_Limit_Switch.GND, Pico.pin_24, https_//github_com/rodolfokeesey/Liquid-Handler.1
  N11: Rear_Limit_Switch.GND, Pico.pin_25, SideKick_V1.1
  N12: Upper_Stepper_Motor.A, JP18.1, Upper_Driver.A2
  N13: Upper_Stepper_Motor.C, JP17.1, Upper_Driver.A1
  N14: Upper_Stepper_Motor.B, Upper_Mot.1, Upper_Driver.B2
  N15: Upper_Stepper_Motor.D, JP16.1, Upper_Driver.B1
  N16: Lower_Stepper_Motor.A, JP22.1, Lower_Driver.A2
  N17: Lower_Stepper_Motor.C, JP21.1, Lower_Driver.A1
  N18: Lower_Stepper_Motor.B, Lower_Mot.1, Lower_Driver.B2
  N19: Lower_Stepper_Motor.D, JP20.1, Lower_Driver.B1
  N20: Purge_Button.4, Pico.pin_26, Schrier_Lab_Fordham_University.1
  N21: Pico.pin_1, Upper_Driver.Dir
  N22: Pico.pin_2, Upper_Driver.Step
  N23: Pico.pin_4, Upper_Driver.CLK
  N24: Pico.pin_5, Upper_Driver.PDN1
  N25: Pico.pin_6, Upper_Driver.PDN2
  N26: Pico.pin_7, Upper_Driver.MS2
  N27: Pico.pin_9, Upper_Driver.MS1
  N28: Pico.pin_10, Upper_Driver.EN
  N29: Pico.pin_11, Upper_Driver.DIAG
  N30: Pico.pin_12, Lower_Driver.Dir
  N31: Pico.pin_14, Lower_Driver.Step
  N32: Pico.pin_15, Lower_Driver.CLK
  N33: Pico.pin_16, Lower_Driver.PDN1
  N34: Pico.pin_17, Lower_Driver.PDN2
  N35: Pico.pin_19, Lower_Driver.MS2
  N36: Pico.pin_20, Lower_Driver.MS1
  N37: Pico.pin_21, Lower_Driver.EN
  N38: Pico.pin_22, Lower_Driver.DIAG
  N39: Pico.pin_30, RUN.1
  N40: Pico.pin_34, GP28.1
  N41: Pico.pin_35, ADC.1
  VDD: Pico.pin_36, Lower_Driver.VDD, Upper_Driver.VDD, 3V3.1
  N42: Pico.pin_37, 3V3_EN.1
  N43: Pico.pin_39, VSS.1
  N44: Pico.pin_40, VBUS.1

custom parts:
  Raspberry Pi Pico: Raspberry Pi Pico. Based around the RP2040 microcontroller the Pico is a low cost microcontroller device bringing Raspberry Pi quality, cost, and easy of use to the microcontroller space. Jan 2021, Split part in to two versions: tht (this one) and SMD. This one will drill holes for a .1 in header in pcb to allow plugging in the module as well as providing pads to solder the module to the top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
  TMC2209: TMC2209-LA stepper motor controller and driver. Supply voltage 4.75-28V Iphase up to 1.77A rms (2.5A peak)
